# Fritzing sketch MotionDetector (saved by Fritzing 0.9.2b)
circuit board: 3.74502cm x 3.3628cm
breadboards: 1

parts:
  PROGR = male pin header, 3 pins [form="♂ (male)"]
  RST = Pushbutton [package="[THT]"]
  POWER = Header 2 [package=jst-2-pth]
  FLASH = Pushbutton [package="[THT]"]
  R1 = Resistor [tolerance=±5% resistance=220 package=THT]
  ESP8266 = ESP8266 WiFi Module [part_number=ESP8266]
  PIR = Header 3 [package=jst-3-pth]

nets:
  N1: PROGR.pin1, ESP8266.TXD
  N2: PROGR.pin2, ESP8266.RXD
  N3: PROGR.pin3, RST.Pin_1, RST.Pin_2, POWER.1, FLASH.Pin_1, FLASH.Pin_2, ESP8266.GND, ESP8266.GPIO_15, PIR.3
  N4: RST.Pin_3, RST.Pin_4, ESP8266.GPIO_16, ESP8266.REST
  N5: POWER.2, ESP8266.VCC, PIR.1
  N6: FLASH.Pin_3, FLASH.Pin_4, ESP8266.GPIO_0
  N7: R1.Pin_0, PIR.2
  N8: R1.Pin_1, ESP8266.GPIO_5

notes:
  MotionDetector_v1.0 - David Lago
  RXD
  GND
  VCC
  OUT
  TXD

custom parts:
  ESP8266 WiFi Module: Generic WiFi Module based on the ESP8266 with onboard PCB antenna and UART communications
